# Fritzing sketch diagram (saved by Fritzing 0.9.3b)
perfboards: 2

parts:
  Part1 = Arduino Nano (Rev3.0) (ICSP)
  Part2 = Real Time Clock Module - DS1307 RTC Breakout Board
  Part3 = Arduino Nano (Rev3.0) (ICSP)
  Part4 = Real Time Clock Module - DS1307 RTC Breakout Board
  S1 = Pushbutton [package="[THT]"]
  S2 = Pushbutton [package="[THT]"]
  R1 = Resistor [tolerance=±5% resistance=10k package="0603 [SMD]"]

nets:
  GND: Part1.GND, Part2.GND
  5V: Part1.5V, Part2.5V
  N1: Part1.A5, Part2.SCL
  N2: Part1.A4, Part2.SDA
  N3: Part3.D11/MOSI, Part3.D12/MISO, S1.Pin_3, S1.Pin_4, S2.Pin_3, S2.Pin_4, R1.Pin_0
  N4: Part3.A5, Part4.SCL
  N5: Part3.A4, Part4.SDA
  N6: S1.Pin_2, S2.Pin_1, S2.Pin_2

notes:
  OLD
  NEW
